// Logisim project Number Display .circ as structural Verilog: 1 circuit, main circuit main
module main (
  input  A,
  input  B,
  input  C,
  input  D
);

  wire A_out, A_prime_B_prime_C_out, A_prime_B_prime_out, A_prime_C_prime_out, AB_out, AC_out, and_1_out,
       B_out, B_prime_CD_out, B_prime_D_prime_out, BC_prime_D_out, BC_prime_out, BCD_prime_out, BD_out,
       C_out, C_prime_D_prime_out, CD_out, CD_prime_out, D_out, E_out, F_out, G_out, not_1_out, not_2_out,
       not_3_out, not_4_out, not_5_out, not_6_out;

  not not_1 (not_1_out, A);
  not not_2 (not_2_out, B);
  not not_3 (not_3_out, C);
  not not_4 (not_4_out, D);
  not not_5 (not_5_out, B);
  not not_6 (not_6_out, D);
  and AB (AB_out, A, B);
  and AC (AC_out, A, C);
  and and_1 (and_1_out, not_1_out, B);
  and A_prime_C_prime (A_prime_C_prime_out, not_1_out, not_3_out);
  and BD (BD_out, B, D);
  and B_prime_D_prime (B_prime_D_prime_out, not_5_out, not_6_out);
  and BC_prime (BC_prime_out, B, not_3_out);
  and A_prime_B_prime (A_prime_B_prime_out, not_1_out, not_2_out);
  and C_prime_D_prime (C_prime_D_prime_out, not_3_out, not_4_out);
  and CD (CD_out, C, D);
  and CD_prime (CD_prime_out, C, not_4_out);
  and BC_prime_D (BC_prime_D_out, B, not_3_out, D);
  and B_prime_CD (B_prime_CD_out, not_2_out, C, D);
  and BCD_prime (BCD_prime_out, B, C, not_4_out);
  and A_prime_B_prime_C (A_prime_B_prime_C_out, not_1_out, not_2_out, C);
  or u_C (C_out, A, and_1_out, A_prime_C_prime_out, CD_out);
  or u_B (B_out, A, A_prime_B_prime_out, C_prime_D_prime_out, CD_out);
  or u_D (D_out, A, CD_prime_out, BC_prime_D_out, B_prime_D_prime_out, B_prime_CD_out);
  or u_A (A_out, A, BD_out, C, B_prime_D_prime_out);
  or F (F_out, A, BC_prime_out, C_prime_D_prime_out, BCD_prime_out);
  or E (E_out, CD_prime_out, AB_out, AC_out, B_prime_D_prime_out);
  or G (G_out, A, CD_prime_out, BC_prime_out, A_prime_B_prime_C_out);
  _7_Segment_Display u_7_segment_display_1 (
    .g(G_out), .f(F_out), .a(A_out), .b(B_out), .e(E_out), .d(D_out), .c(C_out));  // open: dp

  // Notes on the sheet:
  //   A'B
endmodule
