// Logisim project Traffic Lights 2.circ as structural Verilog: 1 circuit, main circuit main
module main (
  input  in_1,
  input  in_2
);

  wire and_1_out, and_2_out, and_3_out, and_4_out, and_5_out, and_6_out, and_7_out, and_8_out, and_9_out,
       and_10_out, clock_1_out, j_k_ff_1_q, j_k_ff_1_qn, j_k_ff_2_q, j_k_ff_2_qn, j_k_ff_3_q, j_k_ff_3_qn;

  Clock clock_1 (.out(clock_1_out));
  and and_1 (and_1_out, j_k_ff_2_q, j_k_ff_3_q);
  and and_2 (and_2_out, j_k_ff_2_q, j_k_ff_3_q);
  J_K_Flip_Flop j_k_ff_1 (
    .J(and_1_out), .clk(clock_1_out), .K(and_2_out), .Q(j_k_ff_1_q), .Qn(j_k_ff_1_qn));  // open: preset, en, reset
  J_K_Flip_Flop j_k_ff_2 (
    .J(j_k_ff_3_q), .clk(clock_1_out), .K(j_k_ff_3_q), .Q(j_k_ff_2_q), .Qn(j_k_ff_2_qn));  // open: preset, en, reset
  J_K_Flip_Flop j_k_ff_3 (
    .J(in_1), .clk(clock_1_out), .K(in_2), .Q(j_k_ff_3_q), .Qn(j_k_ff_3_qn));  // open: preset, en, reset
  and and_3 (and_3_out, j_k_ff_1_qn, j_k_ff_2_qn, j_k_ff_3_qn);
  and and_4 (and_4_out, j_k_ff_1_qn, j_k_ff_2_qn, j_k_ff_3_q);
  and and_5 (and_5_out, j_k_ff_1_qn, j_k_ff_2_q, j_k_ff_3_qn);
  and and_6 (and_6_out, j_k_ff_1_qn, j_k_ff_2_q, j_k_ff_3_q);
  and and_7 (and_7_out, j_k_ff_1_q, j_k_ff_2_qn, j_k_ff_3_qn);
  and and_8 (and_8_out, j_k_ff_1_q, j_k_ff_2_qn, j_k_ff_3_q);
  and and_9 (and_9_out, j_k_ff_1_q, j_k_ff_2_q, j_k_ff_3_qn);
  and and_10 (and_10_out, j_k_ff_1_q, j_k_ff_2_q, j_k_ff_3_q);
  LED led_1 (.in(and_3_out));
  LED led_2 (.in(and_4_out));
  LED led_3 (.in(and_6_out));
  LED led_4 (.in(and_5_out));
  LED led_5 (.in(and_7_out));
  LED led_6 (.in(and_8_out));
  LED led_7 (.in(and_10_out));
  LED led_8 (.in(and_9_out));

  // Notes on the sheet:
  //   2
  //   1
endmodule
